// Logisim project logisim_project.circ as structural Verilog: 4 circuits, main circuit main
module main (
);

  wire CLOCK_out, d_ff_1_q, d_ff_1_qn, n4bit_alu_1_carry, n4bit_alu_1_zero, t_ff_1_q, t_ff_2_q, undriven,
       undriven_2, undriven_3, undriven_4, undriven_5, undriven_6, undriven_7, undriven_8, undriven_9,
       undriven_10, undriven_11, undriven_12, undriven_13, undriven_14, undriven_15;
  wire [3:0] ALU_A_q, ALU_B_q, ALU_OP_q, controlled_buffer_1_out, demultiplexer_1_out0, demultiplexer_1_out1,
       n4bit_alu_1_result, PROGRAM_ADDRESS_A_q, PROGRAM_ADDRESS_B_q, PROGRAM_ADDRESS_C_q, RAM_ADDRESS_q,
       RESULT_q, rom_1_data, rom_1_data_2, ROM_DATA_q;
  wire [11:0] PROGRAM_COUNTER_q;

  Register #(.width(4)) PROGRAM_ADDRESS_A (
    .D(controlled_buffer_1_out), .en(undriven_2), .Q(PROGRAM_ADDRESS_A_q), .clk(d_ff_1_qn));  // open: clr
  Register #(.width(4)) PROGRAM_ADDRESS_B (
    .D(controlled_buffer_1_out), .en(undriven_5), .Q(PROGRAM_ADDRESS_B_q), .clk(d_ff_1_qn));  // open: clr
  Register #(.width(4)) PROGRAM_ADDRESS_C (
    .D(controlled_buffer_1_out), .en(undriven_6), .Q(PROGRAM_ADDRESS_C_q), .clk(d_ff_1_qn));  // open: clr
  Register #(.width(4)) ROM_DATA (
    .D(demultiplexer_1_out1), .en(undriven_3), .Q(ROM_DATA_q), .clk(d_ff_1_qn));  // open: clr
  Register #(.width(4)) ALU_A (
    .D(controlled_buffer_1_out), .en(undriven_4), .Q(ALU_A_q), .clk(d_ff_1_qn));  // open: clr
  Register #(.width(4)) ALU_B (.D(controlled_buffer_1_out), .en(undriven), .Q(ALU_B_q), .clk(d_ff_1_qn));  // open: clr
  Register #(.width(4)) RAM_ADDRESS (
    .D(controlled_buffer_1_out), .en(undriven_11), .Q(RAM_ADDRESS_q), .clk(d_ff_1_qn));  // open: clr
  D_Flip_Flop d_ff_1 (.clk(CLOCK_out), .D(d_ff_1_qn), .Q(d_ff_1_q), .Qn(d_ff_1_qn));  // open: preset, en, reset
  Clock CLOCK (.out(CLOCK_out));
  assign controlled_buffer_1_out = t_ff_1_q ? ROM_DATA_q : 4'bz;  // Controlled_Buffer controlled_buffer_1
  T_Flip_Flop t_ff_1 (.clk(d_ff_1_qn), .T(undriven_8), .Q(t_ff_1_q));  // open: Qn, preset, reset, en
  Register #(.width(4)) ALU_OP (
    .D(controlled_buffer_1_out), .en(undriven_7), .Q(ALU_OP_q), .clk(d_ff_1_qn));  // open: clr
  _4bit_ALU u_4bit_alu_1 (
    .A(ALU_A_q), .B(ALU_B_q), .Result(n4bit_alu_1_result), .Op(ALU_OP_q), .Zero(n4bit_alu_1_zero),
    .Carry(n4bit_alu_1_carry));
  Register #(.width(4)) RESULT (.D(n4bit_alu_1_result), .en(undriven_9), .Q(RESULT_q), .clk(d_ff_1_qn));  // open: clr
  RAM #(.addrWidth(4), .dataWidth(4)) ram_1 (
    .addr(RAM_ADDRESS_q), .data(controlled_buffer_1_out), .sel(undriven_14), .clk(d_ff_1_qn), .ld(undriven_10));  // open: clr
  Counter #(.width(12), .max('hfff)) PROGRAM_COUNTER (
    .D({PROGRAM_ADDRESS_C_q, PROGRAM_ADDRESS_B_q, PROGRAM_ADDRESS_A_q}), .count(undriven_12),
    .Q(PROGRAM_COUNTER_q), .clk(d_ff_1_q));  // open: load, carry, clr
  assign controlled_buffer_1_out = t_ff_2_q ? RESULT_q : 4'bz;  // Controlled_Buffer controlled_buffer_2
  T_Flip_Flop t_ff_2 (.clk(d_ff_1_qn), .T(undriven_13), .Q(t_ff_2_q));  // open: Qn, preset, reset, en
  ROM #(.addrWidth(12)) rom_1 (.addr(PROGRAM_COUNTER_q), .data({rom_1_data_2, rom_1_data}), .sel(1'b1));
  Demultiplexer #(.width(4), .disabled(0), .enable("false")) demultiplexer_1 (
    .out0(demultiplexer_1_out0), .out1(demultiplexer_1_out1), .in(rom_1_data_2), .sel(undriven_15));

  // Notes on the sheet:
  //   TODO DECODER
endmodule

module _1bit_ALU (
  input  Sub,
  input  Cin,
  input  [3:0] Sel,
  input  A,
  input  B,
  input  Less,
  output Result,
  output Cout,
  output Set
);

  wire and_1_out, nor_1_out, or_1_out, xor_1_out, xor_2_out;

  and and_1 (and_1_out, A, B);
  or or_1 (or_1_out, A, B);
  nor nor_1 (nor_1_out, A, B);
  xor xor_1 (xor_1_out, A, B);
  Adder #(.width(1)) adder_1 (.a(A), .b(xor_2_out), .out(Set), .cin(Cin), .cout(Cout));
  xor xor_2 (xor_2_out, B, Sub);
  Multiplexer #(.select(4), .enable("false")) multiplexer_1 (
    .in0(and_1_out), .in1(or_1_out), .in2(nor_1_out), .in3(xor_1_out), .in4(Set), .in5(Less), .in15(Set),
    .out(Result), .sel(Sel));  // open: in6, in7, in8, in9, in10, in11, in12, in13, in14
endmodule

module _4bit_ALU (
  input  [3:0] Op,
  input  [3:0] A,
  input  [3:0] B,
  output [3:0] Result,
  output Zero,
  output Carry
);

  wire and_1_out, n1bit_alu_1_cout, n1bit_alu_2_cout, n1bit_alu_3_cout, n1bit_alu_4_set;

  and and_1 (and_1_out, Op[0], Op[1], Op[2], Op[3]);
  _1bit_ALU u_1bit_alu_1 (
    .A(A[0]), .B(B[0]), .Less(n1bit_alu_4_set), .Result(Result[0]), .Sub(and_1_out), .Cin(and_1_out),
    .Sel(Op), .Cout(n1bit_alu_1_cout));  // open: Set
  _1bit_ALU u_1bit_alu_2 (
    .A(A[1]), .B(B[1]), .Less(1'b0), .Result(Result[1]), .Sub(and_1_out), .Cin(n1bit_alu_1_cout), .Sel(Op),
    .Cout(n1bit_alu_2_cout));  // open: Set
  _1bit_ALU u_1bit_alu_3 (
    .A(A[2]), .B(B[2]), .Less(1'b0), .Result(Result[2]), .Sub(and_1_out), .Cin(n1bit_alu_2_cout), .Sel(Op),
    .Cout(n1bit_alu_3_cout));  // open: Set
  _1bit_ALU u_1bit_alu_4 (
    .A(A[3]), .B(B[3]), .Less(1'b0), .Result(Result[3]), .Sub(and_1_out), .Cin(n1bit_alu_3_cout), .Sel(Op),
    .Cout(Carry), .Set(n1bit_alu_4_set));
  nand nand_1 (Zero, Result[3], Result[2], Result[1], Result[0]);
endmodule

module DECODER (
  input  [3:0] INSTRUCTION,
  input  [3:0] DATA,
  output PROGRAM_COUNTER_WRITE,
  output PROGRAM_ADDRESS_REGISTER_C_WRITE,
  output PROGRAM_ADDRESS_REGISTER_B_WRITE,
  output PROGRAM_ADDRESS_REGISTER_A_WRITE,
  output ROM_DATA_REGISTER_WRITE,
  output ALU_B_REGISTER_WRITE,
  output ALU_A_REGISTER_WRITE,
  output ALU_OPERATION_REGISTER_WRITE,
  output ALU_RESULT_REGISTER_WRITE,
  output RAM_ADDRESS_REGISTER_WRITE,
  output LOAD_RAM_DATA_TO_BUS,
  output SELECT_RAM,
  output TOGGLE_ROM_DATA_BUS_CONNECTION,
  output TOGGLE_ALU_RESULT_BUS_CONNECTION,
  output DATA_SWITCH
);

  wire and_12_out, and_14_out, not_1_out, not_2_out, not_3_out, not_4_out, not_6_out, not_7_out, not_8_out,
       not_9_out;

  and and_1 (PROGRAM_COUNTER_WRITE, and_12_out, not_1_out, not_3_out, not_2_out, not_4_out);
  and and_2 (PROGRAM_ADDRESS_REGISTER_C_WRITE, and_12_out, not_1_out, not_3_out, DATA[1], DATA[0]);
  and and_3 (PROGRAM_ADDRESS_REGISTER_B_WRITE, and_12_out, not_1_out, not_3_out, DATA[1], not_4_out);
  and and_4 (PROGRAM_ADDRESS_REGISTER_A_WRITE, and_12_out, not_1_out, not_3_out, not_2_out, DATA[0]);
  and and_5 (ALU_B_REGISTER_WRITE, and_12_out, not_1_out, DATA[2], not_2_out, DATA[0]);
  and and_6 (ALU_A_REGISTER_WRITE, and_12_out, not_1_out, DATA[2], not_2_out, not_4_out);
  and and_7 (ALU_OPERATION_REGISTER_WRITE, and_12_out, not_1_out, DATA[2], DATA[1], not_4_out);
  and and_8 (ALU_RESULT_REGISTER_WRITE, and_12_out, not_1_out, DATA[2], DATA[1], DATA[0]);
  and and_9 (RAM_ADDRESS_REGISTER_WRITE, and_12_out, DATA[3], not_3_out, not_2_out, not_4_out);
  and and_10 (TOGGLE_ROM_DATA_BUS_CONNECTION, and_14_out, not_1_out, not_3_out, not_2_out, not_4_out);
  and and_11 (TOGGLE_ALU_RESULT_BUS_CONNECTION, and_14_out, not_1_out, not_3_out, not_2_out, DATA[0]);
  not not_1 (not_1_out, DATA[3]);
  not not_2 (not_2_out, DATA[1]);
  not not_3 (not_3_out, DATA[2]);
  not not_4 (not_4_out, DATA[0]);
  and and_12 (and_12_out, not_6_out, INSTRUCTION[1], not_8_out, not_9_out);
  and and_13 (ROM_DATA_REGISTER_WRITE, INSTRUCTION[0], INSTRUCTION[1], not_8_out, not_9_out);
  and and_14 (and_14_out, INSTRUCTION[0], not_7_out, not_8_out, not_9_out);
  not not_5 (DATA_SWITCH, and_12_out);
  not not_6 (not_6_out, INSTRUCTION[0]);
  not not_7 (not_7_out, INSTRUCTION[1]);
  not not_8 (not_8_out, INSTRUCTION[2]);
  not not_9 (not_9_out, INSTRUCTION[3]);

  // Notes on the sheet:
  //   WRITE TO ROM REGISTER
  //   TOGGLE BUS CONNECTION
  //   WRITE TO REGISTER
endmodule
